# Fritzing sketch Visual Metronome (saved by Fritzing 0.9.3b)

parts:
  Arduino_Uno = Arduino Uno (Rev3)
  Adafruit_Neopixel_Ring = 12 NeoPixel Ring

nets:
  N1: Arduino_Uno.D6_PWM, Adafruit_Neopixel_Ring.IN
  5V: Arduino_Uno.5V, Adafruit_Neopixel_Ring.VDD
  GND: Arduino_Uno.GND, Adafruit_Neopixel_Ring.GND

custom parts:
  12 NeoPixel Ring: 12 ultra bright smart LED NeoPixels are arranged in a circle with 1.5" (37mm) outer diameter. The rings are 'chainable' - connect the output pin of one to the input pin of another. Use only one microcontroller pin to control as many as you can chain together! Each LED is addressable as the driver chip is inside the LED. Each one has ~18mA constant current drive so the color will be very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
